# Fritzing sketch 2019-01-25-esp8266-programming-fritzing (saved by Fritzing 0.9.3b)
breadboards: 1

parts:
  U2 = ESP8266 WiFi Module [part_number=ESP8266]
  Part1 = FTDI Basic Programmer
  Power_plug1 = Power plug
  S1 = Pushbutton [package="[THT]"]
  S2 = Pushbutton [package="[THT]"]
  R1 = Resistor [tolerance=±5% resistance=100 package="2512 [SMD]"]
  R2 = Resistor [tolerance=±5% resistance=100 package="2512 [SMD]"]

nets:
  N1: U2.RXD, Part1.TXO
  VCC: U2.VCC, Power_plug1.VCC, R1.Pin_0, R2.Pin_0
  N2: U2.GPIO_0, S1.Pin_1, S1.Pin_2
  N3: U2.RST, S2.Pin_1, S2.Pin_2, R1.Pin_1
  N4: U2.CH_PD, R2.Pin_1
  GND: U2.GND, Part1.GND, Power_plug1.GND, S1.Pin_3, S1.Pin_4, S2.Pin_3, S2.Pin_4
  N5: U2.TXD, Part1.RXI

notes:
  +3.3V (do NOT use +5V)
  Reset
  Mode
  (GPIO0 to GND)
  FTDI
  (Serial to USB)

custom parts:
  ESP8266 WiFi Module: Generic WiFi Module based on the ESP8266 with onboard PCB antenna and UART communications
